// Logisim project counter.circ as structural Verilog: 1 circuit, main circuit main
module main (
  input  in_1,
  input  in_2,
  output [31:0] out_3
);

  wire adder_1_cout, CLK;
  wire [31:0] adder_1_out;

  Clock clock_1 (.out(CLK));
  Adder #(.width(32)) adder_1 (.a(32'h1), .b(out_3), .out(adder_1_out), .cin(1'b0), .cout(adder_1_cout));
  Register #(.width(32)) register_1 (.D(adder_1_out), .en(in_1), .clk(CLK), .Q(out_3), .clr(in_2));
  // also tied to GND on the sheet: adder_1_cout

  // Other names for the same wires on the sheet: ENABLE = in_1; RESET = in_2

  // Notes on the sheet:
  //   32bit COUNTER
endmodule
