// Logisim project frequency_div.circ as structural Verilog: 1 circuit, main circuit main
module main (
  input  enable,
  input  rst,
  output clk_out
);

  wire and_1_out, clk_in_out, comparator_1_eq, not_1_out;
  wire [3:0] adder_1_out, multiplexer_1_out, register_1_q;

  Adder #(.width(4)) adder_1 (.a(4'b0001), .b(register_1_q), .out(adder_1_out));  // open: cin, cout
  Clock clk_in (.out(clk_in_out));
  // Digital_Oscilloscope #(.nState(20)) digital_oscilloscope_1: pin names not known; wires that end beside it: clk_in_out, clk_out
  Multiplexer #(.select(4), .width(4)) multiplexer_1 (
    .in0(adder_1_out), .in1(adder_1_out), .in2(adder_1_out), .in3(adder_1_out), .in4(adder_1_out),
    .in5(adder_1_out), .in6(adder_1_out), .in7(adder_1_out), .in8(adder_1_out), .in9(4'b0000),
    .in10(adder_1_out), .in11(adder_1_out), .in12(adder_1_out), .in13(adder_1_out), .in14(adder_1_out),
    .in15(adder_1_out), .out(multiplexer_1_out), .sel(register_1_q));
  Register #(.width(4)) register_1 (.D(multiplexer_1_out), .en(enable), .clk(clk_in_out), .Q(register_1_q), .clr(rst));
  Comparator #(.width(4)) comparator_1 (.a(register_1_q), .b(4'b0000), .eq(comparator_1_eq));  // open: gt, lt
  not not_1 (not_1_out, rst);
  and and_1 (and_1_out, comparator_1_eq, not_1_out);
  and and_2 (clk_out, and_1_out, enable);

  // Notes on the sheet:
  //   Frequency Divider
endmodule
