// Logisim project fsm.circ as structural Verilog: 1 circuit, main circuit main
// state
module main (
  input  in_1,
  input  in_2,
  input  rst,
  input  [31:0] a,
  input  [31:0] b
);

  wire clk_out, mul_cnt_q, multiplexer_6_out, not_1_out;
  wire [2:0] multiplexer_3_out, multiplexer_4_out, multiplexer_5_out, state_q;
  wire [31:0] multiplexer_1_out, multiplexer_2_out, shifter_1_out, subtractor_1_out;
  wire [34:0] multiplexer_7_out, undriven;

  Clock clk (.out(clk_out));
  Register #(.width(1)) mul_cnt (.D(not_1_out), .en(1'b1), .clk(clk_out), .Q(mul_cnt_q), .clr(rst));
  not not_1 (not_1_out, mul_cnt_q);
  Multiplexer #(.select(3), .width(32)) multiplexer_1 (
    .in0(a), .in1(b), .in2({32{1'b0}}), .in3({32{1'b0}}), .in4({32{1'b0}}), .in5({32{1'b0}}),
    .in6({32{1'b0}}), .in7({32{1'b0}}), .out(multiplexer_1_out), .sel(state_q));
  Shifter #(.shift("lr"), .width(32)) shifter_1 (.in(multiplexer_1_out), .\dist (5'b00001), .out(shifter_1_out));
  Multiplexer #(.select(3), .width(32)) multiplexer_2 (.out(multiplexer_2_out));  // open: in0, in1, in2, in3, in4, in5, in6, in7, sel
  Multiplexer #(.width(3)) multiplexer_3 (.in0(3'b100), .in1(3'b011), .out(multiplexer_3_out), .sel(mul_cnt_q));
  Multiplexer #(.width(3)) multiplexer_4 (.in0(3'b101), .in1(3'b100), .out(multiplexer_4_out), .sel(mul_cnt_q));
  Multiplexer #(.select(3), .width(3)) multiplexer_5 (
    .in0(3'b001), .in1(3'b010), .in2(3'b011), .in3(multiplexer_3_out), .in4(multiplexer_4_out), .in5(3'b000),
    .in6(3'b000), .in7(3'b000), .out(multiplexer_5_out), .sel(state_q));
  Subtractor #(.width(32)) subtractor_1 (.a(a), .b(multiplexer_2_out), .out(subtractor_1_out));  // open: bin, bout
  Register #(.width(3)) state (.D(multiplexer_5_out), .en(multiplexer_6_out), .Q(state_q), .clr(rst));  // open: clk
  Multiplexer multiplexer_6 (.in0(1'b1), .in1(1'b0), .out(multiplexer_6_out));  // open: sel
  Multiplexer #(.select(3), .width(35)) multiplexer_7 (
    .in0({35{1'b0}}), .in1({3'b000, shifter_1_out}), .in2({3'b000, subtractor_1_out}), .in3({35{1'b0}}),
    .in4(undriven), .in5({35{1'b0}}), .in6({35{1'b0}}), .in7({35{1'b0}}), .out(multiplexer_7_out),
    .sel(state_q));
  Register #(.width(35)) reg2 (.D(multiplexer_7_out));  // open: en, clk, Q, clr

  // Notes on the sheet:
  //   div2
endmodule
