// Logisim project shift_right.circ as structural Verilog: 1 circuit, main circuit main
module main (
  input  [31:0] data_in,
  input  rst,
  input  load,
  input  shift_enable,
  output serial_out,
  output [31:0] out_6
);

  wire digital_oscilloscope_1_p1, multiplexer_2_out, multiplexer_3_out;
  wire [31:0] data_in_reg_q, multiplexer_1_out;

  // Digital_Oscilloscope #(.nState(32)) digital_oscilloscope_1: pin names not known; wires that end beside it: digital_oscilloscope_1_p1, serial_out
  Clock clk (.out(digital_oscilloscope_1_p1));
  Multiplexer #(.width(32)) multiplexer_1 (
    .in0({data_in_reg_q[30:0], 1'b0}), .in1(data_in), .out(multiplexer_1_out), .sel(load));
  Multiplexer multiplexer_2 (.in0(shift_enable), .in1(1'b1), .out(multiplexer_2_out), .sel(load));
  Register #(.width(32)) data_in_reg (
    .D(multiplexer_1_out), .en(multiplexer_2_out), .clk(digital_oscilloscope_1_p1), .Q(data_in_reg_q),
    .clr(rst));
  Multiplexer multiplexer_3 (.in0(shift_enable), .in1(1'b0), .out(multiplexer_3_out), .sel(load));
  Register #(.width(1)) serial_out_reg (
    .D(data_in_reg_q[31]), .en(multiplexer_3_out), .clk(digital_oscilloscope_1_p1), .Q(serial_out), .clr(rst));
  Register #(.width(32)) register_1 (
    .D({serial_out, out_6[31:1]}), .en(multiplexer_3_out), .clk(digital_oscilloscope_1_p1), .Q(out_6),
    .clr(rst));

  // Notes on the sheet:
  //   Rigth shift register
endmodule
