// Logisim project subtractor.circ as structural Verilog: 1 circuit, main circuit main
module main (
  input  [34:0] in_1,
  input  [34:0] in_2,
  output [34:0] out_3
);

  wire [34:0] adder_1_out, not_1_out;

  assign not_1_out = ~in_2;  // NOT_Gate not_1, 35 bits wide
  Adder #(.width(35)) adder_1 (.a(in_1), .b(not_1_out), .out(adder_1_out));  // open: cin, cout
  Adder #(.width(35)) adder_2 (.a(35'h1), .b(adder_1_out), .out(out_3));  // open: cin, cout

  // Notes on the sheet:
  //   Subtractor
endmodule
